# Fritzing sketch BME280 (saved by Fritzing 0.9.3b)

parts:
  Raspberry_Pi_Zero1 = Raspberry Pi Zero
  Part1 = Adafruit BME280

nets:
  3V3: Raspberry_Pi_Zero1.3v3, Part1.VIN
  N1: Raspberry_Pi_Zero1.GPIO2, Part1.SDI/SDA
  N2: Raspberry_Pi_Zero1.GPIO3, Part1.SCK/SCL
  GND: Raspberry_Pi_Zero1.GND, Part1.GND

custom parts:
  Adafruit BME280: Bosch has stepped up their game with their new BME280 sensor, an environmental sensor with temperature, barometric pressure and humidity! This sensor is great for all sorts of weather/environmental sensing and can even be used in both I2C and SPI! This precision sensor from Bosch is the best low-cost sensing solution for measuring humidity with ±3% accuracy, barometric pressure with ±1 hPa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
