# Fritzing sketch MCP9808 (saved by Fritzing 0.9.3b)
breadboards: 1

parts:
  Part1 = MCP9808 High Accuracy I2C Temperature Sensor [part_number=1782]
  Raspberry_Pi_Zero1 = Raspberry Pi Zero

nets:
  3V3: Part1.VDD, Raspberry_Pi_Zero1.3v3, Raspberry_Pi_Zero1.3V3, Raspberry_Pi_Zero1.GPIO24
  GND: Part1.GND, Part1.SCL, Raspberry_Pi_Zero1.GPIO3, Raspberry_Pi_Zero1.GND, Raspberry_Pi_Zero1.GPIO27, Raspberry_Pi_Zero1.GPIO10, Raspberry_Pi_Zero1.GPIO5, Raspberry_Pi_Zero1.GPIO13, Raspberry_Pi_Zero1.GPIO21, Raspberry_Pi_Zero1.GPIO7, Raspberry_Pi_Zero1.GPIO15
  N1: Part1.SDA, Raspberry_Pi_Zero1.GPIO2, Raspberry_Pi_Zero1.5V
  N2: Raspberry_Pi_Zero1.GPIO4, Raspberry_Pi_Zero1.GPIO14
  N3: Raspberry_Pi_Zero1.GPIO17, Raspberry_Pi_Zero1.GPIO18
  N4: Raspberry_Pi_Zero1.GPIO22, Raspberry_Pi_Zero1.GPIO23
  N5: Raspberry_Pi_Zero1.GPIO9, Raspberry_Pi_Zero1.GPIO25
  N6: Raspberry_Pi_Zero1.GPIO11, Raspberry_Pi_Zero1.GPIO8
  N7: Raspberry_Pi_Zero1.ID_SD, Raspberry_Pi_Zero1.ID_SC
  N8: Raspberry_Pi_Zero1.GPIO6, Raspberry_Pi_Zero1.GPIO12
  N9: Raspberry_Pi_Zero1.GPIO19, Raspberry_Pi_Zero1.GPIO16
  N10: Raspberry_Pi_Zero1.GPIO26, Raspberry_Pi_Zero1.GPIO20

custom parts:
  MCP9808 High Accuracy I2C Temperature Sensor: This I2C digital temperature sensor is one of the more accurate/precise we've ever seen, with a typical accuracy of ±0.25°C over the sensor's -40°C to +125°C range and precision of +0.0625°C. They work great with any microcontroller using standard i2c. There are 3 address pins so you can connect up to 8 to a single I2C bus without address collisions. Best of all, a wide voltage range makes is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
