# Fritzing sketch Si7021 (saved by Fritzing 0.9.3b)
breadboards: 1

parts:
  Raspberry_Pi_Zero1 = Raspberry Pi Zero
  Part1 = Adafruit Si7021 Temp Humidity [part_number="Adafruit #3251"]

nets:
  3V3: Raspberry_Pi_Zero1.3v3, Raspberry_Pi_Zero1.3V3, Raspberry_Pi_Zero1.GPIO24, Part1.VIN
  N1: Raspberry_Pi_Zero1.GPIO2, Raspberry_Pi_Zero1.5V, Part1.SDA
  GND: Raspberry_Pi_Zero1.GPIO3, Raspberry_Pi_Zero1.GND, Raspberry_Pi_Zero1.GPIO27, Raspberry_Pi_Zero1.GPIO10, Raspberry_Pi_Zero1.GPIO5, Raspberry_Pi_Zero1.GPIO13, Raspberry_Pi_Zero1.GPIO21, Raspberry_Pi_Zero1.GPIO7, Raspberry_Pi_Zero1.GPIO15, Part1.SCL, Part1.GND
  N2: Raspberry_Pi_Zero1.GPIO4, Raspberry_Pi_Zero1.GPIO14
  N3: Raspberry_Pi_Zero1.GPIO17, Raspberry_Pi_Zero1.GPIO18
  N4: Raspberry_Pi_Zero1.GPIO22, Raspberry_Pi_Zero1.GPIO23
  N5: Raspberry_Pi_Zero1.GPIO9, Raspberry_Pi_Zero1.GPIO25
  N6: Raspberry_Pi_Zero1.GPIO11, Raspberry_Pi_Zero1.GPIO8
  N7: Raspberry_Pi_Zero1.ID_SD, Raspberry_Pi_Zero1.ID_SC
  N8: Raspberry_Pi_Zero1.GPIO6, Raspberry_Pi_Zero1.GPIO12
  N9: Raspberry_Pi_Zero1.GPIO19, Raspberry_Pi_Zero1.GPIO16
  N10: Raspberry_Pi_Zero1.GPIO26, Raspberry_Pi_Zero1.GPIO20

custom parts:
  Adafruit Si7021 Temp Humidity: It's summer and you're sweating and your hair's all frizzy and all you really want to know is why the weatherman said this morning that today's relative humidity would max out at a perfectly reasonable 42% when it feels more like 77%. Enter the Si7021 Temperature + Humidity Sensor - the best way to prove the weatherman wrong! This lovely sensor for Silicon labs has ± 3% relative humidity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
