# Fritzing sketch battery-and-regulator (saved by Fritzing 0.9.3b)

parts:
  U1 = Voltage Regulator - 5V [package="TO220 [THT]"]
  Raspberry_Pi_Zero1 = Raspberry Pi Zero
  U2 = LIPO-1000mAh [package=lipo-1000]

nets:
  N1: U1.input_voltage, U2.+
  GND: U1.GND, Raspberry_Pi_Zero1.GPIO14, Raspberry_Pi_Zero1.GND, U2.-
  N2: U1.output_voltage, Raspberry_Pi_Zero1.5V
