# Fritzing sketch dotstar-simple (saved by Fritzing 0.9.3b)

parts:
  Raspberry_Pi_Zero1 = Raspberry Pi Zero
  LPD8806_RGB_LED_Strip1 = LPD8806 RGB LED Strip
  J1 = Power Jack [package=power_jack_combo]

nets:
  GND: Raspberry_Pi_Zero1.GND, Raspberry_Pi_Zero1.GPIO10, LPD8806_RGB_LED_Strip1.GND, LPD8806_RGB_LED_Strip1.DI, J1.GND
  N1: Raspberry_Pi_Zero1.GPIO11, Raspberry_Pi_Zero1.GPIO8, LPD8806_RGB_LED_Strip1.CI
  N2: LPD8806_RGB_LED_Strip1.+5V, J1.GNDBREAK

custom parts:
  LPD8806 RGB LED Strip: Digitally addressable RGB LED strip
