# Fritzing sketch led-and-button (saved by Fritzing 0.9.3b)
breadboards: 1

parts:
  LED1 = LED - 5mm [color="Red (633nm)" package="5 mm [THT]"]
  S2 = Pushbutton [package="[THT]"]
  Raspberry_Pi_Zero1 = Raspberry Pi Zero
  R1 = Resistor [tolerance=±5% resistance=220 package=THT]
  R2 = Resistor [tolerance=±5% resistance=10k package=THT]

nets:
  N1: LED1.cathode, R1.Pin_1
  N2: LED1.anode, Raspberry_Pi_Zero1.GPIO14
  N3: S2.Pin_1, S2.Pin_2, Raspberry_Pi_Zero1.GPIO15, R2.Pin_0
  N4: S2.Pin_3, S2.Pin_4, Raspberry_Pi_Zero1.3v3
  N5: Raspberry_Pi_Zero1.GND, R1.Pin_0, R2.Pin_1
