# Fritzing sketch neopixel-74LVC245 (saved by Fritzing 0.9.3b)
breadboards: 1

parts:
  Part1 = NeoPixel Jewel [part_number=2226]
  Raspberry_Pi_Zero1 = Raspberry Pi Zero
  J1 = Power Jack [package=power_jack_smd]
  IC1 = 74LVC245 Octal 2-Way Tranceiver
  C1 = Electrolytic Capacitor [capacitance=1mF package="100 mil [THT, electrolytic]"]

nets:
  GND: Part1.GND, Raspberry_Pi_Zero1.GND, IC1.!OE, C1.-
  N1: Part1.IN, IC1.B1
  VDD: Part1.VDD, J1.PWR, IC1.DIR, IC1.VCC, C1.+
  N2: Raspberry_Pi_Zero1.GPIO18, IC1.A1

custom parts:
  NeoPixel Jewel: We fit seven of our tiny 5050 (5mm x 5mm) smart RGB LEDs onto a beautiful, round PCB with mounting holes and a chainable design to create what we think is our most elegant (and evening-wear appropriate) NeoPixel board yet. Use only one microcontroller pin to control as many as you can chain together! Each LED is addressable as the driver chip is inside the LED. Each one has ~18mA constant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
  74LVC245 Octal 2-Way Tranceiver: 74LVC245 Octal Bi-directional Tri-state Transceiver
