# Fritzing sketch neopixel-simpl (saved by Fritzing 0.9.3b)

parts:
  Part1 = NeoPixel Jewel [part_number=2226]
  Raspberry_Pi_Zero1 = Raspberry Pi Zero
  J1 = Power Jack [package=power_jack_smd]

nets:
  GND: Part1.GND, Raspberry_Pi_Zero1.GND, J1.GND
  N1: Part1.IN, Raspberry_Pi_Zero1.GPIO18
  N2: Part1.VDD, J1.GNDBREAK

custom parts:
  NeoPixel Jewel: We fit seven of our tiny 5050 (5mm x 5mm) smart RGB LEDs onto a beautiful, round PCB with mounting holes and a chainable design to create what we think is our most elegant (and evening-wear appropriate) NeoPixel board yet. Use only one microcontroller pin to control as many as you can chain together! Each LED is addressable as the driver chip is inside the LED. Each one has ~18mA constant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
