# Fritzing sketch pi-zero-audio-breadboard-nolabels (saved by Fritzing 0.9.3b)
breadboards: 1

parts:
  Part1 = Adafruit Pi Cobbler Plus [part_number="Adafruit #2029"]
  R1 = Resistor [tolerance=±5% resistance=270 package=THT]
  C1 = Ceramic Capacitor [capacitance=10nF package="100 mil [THT, multilayer]"]
  R2 = Resistor [tolerance=±5% resistance=150 package=THT]
  R3 = Resistor [tolerance=±5% resistance=270 package=THT]
  R4 = Resistor [tolerance=±5% resistance=150 package=THT]
  C3 = Ceramic Capacitor [capacitance=10nF package="100 mil [THT, multilayer]"]
  C4 = Electrolytic Capacitor [capacitance=1µF package="100 mil [THT, electrolytic]"]
  C5 = Electrolytic Capacitor [capacitance=1µF package="100 mil [THT, electrolytic]"]

nets:
  N1: Part1.GND, C1.0, R2.Pin_0, R4.Pin_1, C3.1
  N2: Part1.GPIO13, R3.Pin_0
  N3: Part1.GPIO18, R1.Pin_0
  N4: R1.Pin_1, C1.1, R2.Pin_1, C5.+
  N5: R3.Pin_1, R4.Pin_0, C3.0, C4.+

custom parts:
  Adafruit Pi Cobbler Plus: The Raspberry Pi B+/Pi 2/ Pi 3 has landed on the Maker World like a 40-GPIO pinned, quad-USB ported, credit card sized bomb of DIY joy. And while you can use most of our great Model B accessories by hooking up our downgrade cable, its probably a good time to upgrade your set up and accessorize using all of the Model B+'s / Pi 2's / Pi 3's 40 pins. That's why we now carry the Adafruit Assembled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
