# Fritzing sketch pi-zero-audio (saved by Fritzing 0.9.3b)

parts:
  C6 = Electrolytic Capacitor [capacitance=1µF package="100 mil [THT, electrolytic]"]
  R2 = Resistor [tolerance=±5% resistance=270 package=THT]  # not connected
  C7 = Ceramic Capacitor [capacitance=10nF package="100 mil [THT, multilayer]"]
  R3 = Resistor [tolerance=±5% resistance=150 package=THT]
  C8 = Electrolytic Capacitor [capacitance=1µF package="100 mil [THT, electrolytic]"]
  R4 = Resistor [tolerance=±5% resistance=270 package=THT]  # not connected
  R5 = Resistor [tolerance=±5% resistance=150 package=THT]  # not connected
  C9 = Ceramic Capacitor [capacitance=10nF package="100 mil [THT, multilayer]"]
  TRS1 = Audio Jack (TRS) 3.5mm [package="PG203J [THT]"]

nets:
  N1: C6.-, TRS1.Tip
  N2: C7.0, R3.Pin_1, C9.1, TRS1.Sleeve
  N3: C8.-, TRS1.Ring

notes:
  33nF,
  labeled 333
  or 10nF, 103
  Gnd
  RPi pin 18
  RPi pin 13
  270Ω
  1µF
  Add to /boot/config.txt:
  dtoverlay=pwm-2chan,pin=18,func=2,pin2=13,func2=4
  150Ω
  ring
  tip
