# Fritzing sketch plant-watering (saved by Fritzing 0.9.3b)
breadboards: 1

parts:
  IC1 = H-Bridge [package=THT]
  Raspberry_Pi_Zero1 = Raspberry Pi Zero
  M1 = DC Motor
  Part1 = Adafruit ADS1115 16Bit I2C ADC [part_number="Adafruit #1085"]
  Part2 = FC-28 Soil Hygrometer Module

nets:
  N1: IC1.1_2EN, Raspberry_Pi_Zero1.GIPO22, Raspberry_Pi_Zero1.GIPO23
  N2: IC1.1Y, M1.pin_2
  GND: IC1.GND1, IC1.GND2, IC1.2A, IC1.GND3, IC1.GND4, Raspberry_Pi_Zero1.GPIO3, Raspberry_Pi_Zero1.GND, Part1.SCL, Part1.GND, Part2.GND
  N3: IC1.2Y, M1.pin_1
  N4: IC1.VCC2, IC1.VCC1, Raspberry_Pi_Zero1.5V
  3V3: Raspberry_Pi_Zero1.3v3, Part1.VDD, Part2.VCC
  N5: Raspberry_Pi_Zero1.GPIO2, Part1.SDA
  N6: Part1.AIN0, Part2.AO

notes:
  5v pump
  5v rail
  3.3v rail
  YL-38 moisture sensor

custom parts:
  Adafruit ADS1115 16Bit I2C ADC: For microcontrollers without an analog-to-digital converter or when you want a higher-precision ADC, the ADS1115 provides 16-bit precision at 860 samples/second over I2C. The chip can be configured as 4 single-ended input channels, or two differential channels. As a nice bonus, it even includes a programmable gain amplifier, up to x16, to help boost up smaller single/differential signals to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
  FC-28 Soil Hygrometer Module: The FC-28 is a soil hygrometer module that uses the Texas Instruments LM393 comparator chip to provide an analog measurement of soil humidity. The digital output is high when soil moisture is over a certain threshold, as determined by adjusting the potentiometer.
