# Fritzing sketch powerswitch-tail-3wire (saved by Fritzing 0.9.3b)

parts:
  Raspberry_Pi_Zero1 = Raspberry Pi Zero
  SW1 = PowerSwitch Tail II

nets:
  N1: Raspberry_Pi_Zero1.3v3, SW1.+in
  N2: Raspberry_Pi_Zero1.GND, SW1.Ground
  N3: Raspberry_Pi_Zero1.GPIO14, SW1.-in
